# Fritzing sketch Untitled Sketch (saved by Fritzing 0.9.3b)
breadboards: 1

parts:
  U1 = POT [package=pot_alpha_rv16af-20]
  R1 = Rotary Potentiometer (Large) [maximum_resistance=100kΩ package=THT]
  Part1 = Arduino Uno (Rev3) - ICSP
  LED1 = smd LED [color="Red (633nm)" package="0603 [SMD]"]
  R3 = Resistor [tolerance=±5% resistance=220 package="2010 [SMD]"]
  R4 = Resistor [tolerance=±5% resistance=220 package="2010 [SMD]"]
  R5 = Resistor [tolerance=±5% resistance=220 package="2010 [SMD]"]
  R6 = Resistor [tolerance=±5% resistance=220 package="2010 [SMD]"]
  R7 = Resistor [tolerance=±5% resistance=220 package="2010 [SMD]"]
  R8 = Resistor [tolerance=±5% resistance=220 package="2010 [SMD]"]
  LED2 = smd LED [color="Red (633nm)" package="0603 [SMD]"]
  LED3 = smd LED [color="Red (633nm)" package="0603 [SMD]"]
  LED4 = smd LED [color="Red (633nm)" package="0603 [SMD]"]
  LED5 = smd LED [color="Red (633nm)" package="0603 [SMD]"]
  LED6 = smd LED [color="Red (633nm)" package="0603 [SMD]"]
  LED7 = smd LED [color="Red (633nm)" package="0603 [SMD]"]  # not connected
  R9 = Resistor [tolerance=±5% resistance=220 package="2010 [SMD]"]  # not connected

nets:
  N1: U1.A, R1.leg1, Part1.GND, LED1.cathode, LED2.cathode, LED3.cathode, LED4.cathode, LED5.cathode, LED6.cathode
  N2: U1.S, Part1.A0
  N3: U1.E, R1.leg2, Part1.5V
  N4: R1.wiper, Part1.A1
  N5: Part1.D8, R5.Pin_1
  N6: Part1.D9_PWM, R3.Pin_1
  N7: Part1.D10_PWM/SS, R4.Pin_1
  N8: Part1.D5_PWM, R8.Pin_1
  N9: Part1.D6_PWM, R7.Pin_1
  N10: Part1.D7, R6.Pin_1
  N11: LED1.anode, R8.Pin_0
  N12: R3.Pin_0, LED5.anode
  N13: R4.Pin_0, LED6.anode
  N14: R5.Pin_0, LED4.anode
  N15: R6.Pin_0, LED3.anode
  N16: R7.Pin_0, LED2.anode

notes:
  Diodes only allow current to flow in one direction, and they're always polarized. A diode has two terminals. The positive side is called the anode, and the negative one is called the cathode. In this example the resistor is connected to the anode.
  The red and black wires represent the live and ground respectivley. We connect them to the power bank on the breadboard.
